// Logisim project machineREAL.circ as structural Verilog: 31 circuits, main circuit main
module main (
  output out_1
);

  wire _1, _2, _3, _4, c_1_out_3, c_1_out_4, c_1_out_5, c_1_out_7, c_1_out_8, c_1_out_9, c_1_out_10,
       c_1_out_11, high_bit_1_out_4, j_1_jmpc, MDR_flag, n1_bit_flip_fop_1_out_3, n1_bit_flip_fop_2_out_3,
       n4_16_decoder_1_out_2, n4_16_decoder_1_out_3, n4_16_decoder_1_out_4, n4_16_decoder_1_out_5,
       n4_16_decoder_1_out_6, n4_16_decoder_1_out_7, n4_16_decoder_1_out_8, n4_16_decoder_1_out_9,
       n4_16_decoder_1_out_10, n32bit_alu_1_sign, n32bit_alu_1_zero, Read;
  wire [1:0] alu_under_cs_1_shift, j_1_jamn_jamz;
  wire [2:0] J, M, m_1_out_3;
  wire [3:0] B, b_1_out_3;
  wire [5:0] alu_under_cs_1_alu;
  wire [7:0] _8, ALU, MBR, OP_Code, ram_1_mbr;
  wire [8:0] Addr, addr_1_out_3, C, junction_box_1_out_5;
  wire [23:0] MAR, pc_1_ramoutput, store_1_o_mar, store_1_o_pc;
  wire [31:0] B_Bus, C_Bus, CPP, H, LV, MDR, mdr_1_r_input, n32bit_alu_1_output, OPC, PC, ram_1_mdr, SP,
       store_1_o_data, store_1_o_mdr, TOS;

  // Probe on SP
  // Probe on LV
  // Probe on CPP
  // Probe on B_Bus
  // Probe on C_Bus
  Hex_Digit_Display hex_digit_display_1 (.value(OP_Code[7:4]));  // open: dp
  RAM ram_1 (
    .Data(store_1_o_data), .MAR(store_1_o_mar), .MDR(ram_1_mdr), .PC(store_1_o_pc), .MBR(ram_1_mbr),
    .Clock(_3), .Read(m_1_out_3[1]), .Write(m_1_out_3[2]), .Fetch(m_1_out_3[0]), .R_Read(Read),
    .MDR_flag(MDR_flag));
  Master_Clock master_clock_1 (.out_1(_1), .out_2(_2), .out_3(_3), .out_4(_4));
  // Probe on MAR
  // Probe on MDR
  // Probe on MBR
  // Probe on PC
  Hex_Digit_Display hex_digit_display_2 (.value(OP_Code[3:0]));  // open: dp
  // Probe on TOS
  // Probe on OPC
  // Probe on H
  Store store_1 (
    .O_MAR(store_1_o_mar), .I_MDR(ram_1_mdr), .O_Data(store_1_o_data), .O_PC(store_1_o_pc),
    .I_MBR(ram_1_mbr), .I_MAR(MAR), .O_MDR(store_1_o_mdr), .I_Data(mdr_1_r_input), .I_PC(pc_1_ramoutput),
    .O_MBR(_8), .Clock(_3));
  MAR mar_1 (.in_1(C_Bus), .RamOutput(MAR), .in_2(c_1_out_4), .Clock(_2));
  H h_1 (.in_1(C_Bus), .Enable(c_1_out_3), .out_4(H), .Clock(_2));
  // Probe on _8
  MDR mdr_1 (
    .C_Bus(C_Bus), .Enable(MDR_flag), .B_Bus(B_Bus), .Clock(_2), .B_Enable(n4_16_decoder_1_out_2),
    .R_Output(store_1_o_mdr), .R_Input(mdr_1_r_input), .R_Read(Read), .Display(MDR));
  PC pc_1 (
    .in_1(C_Bus), .Enable(c_1_out_8), .out_6(B_Bus), .Clock(_2), .B_Enable(n4_16_decoder_1_out_3),
    .RamOutput(pc_1_ramoutput), .Display(PC));
  MBR mbr_1 (
    .in_2(_8), .out_6(B_Bus), .out_7(B_Bus), .Clock(_2), .B_Enable(n4_16_decoder_1_out_4),
    .B_Enable_2(n4_16_decoder_1_out_5), .Junction_Box(MBR));
  SP sp_1 (
    .in_1(C_Bus), .Enable(c_1_out_10), .out_5(B_Bus), .Clock(_2), .B_Enable(n4_16_decoder_1_out_6),
    .Display(SP));
  LV lv_1 (
    .in_1(C_Bus), .Enable(c_1_out_11), .out_5(B_Bus), .Clock(_2), .B_Enable(n4_16_decoder_1_out_7),
    .Display(LV));
  CPP cpp_1 (
    .in_1(C_Bus), .out_5(B_Bus), .Clock(_2), .B_Enable(n4_16_decoder_1_out_8), .Enable(c_1_out_9),
    .Display(CPP));
  TOS tos_1 (
    .in_1(C_Bus), .Enable(c_1_out_7), .out_5(B_Bus), .Clock(_2), .B_Enable(n4_16_decoder_1_out_9),
    .Display(TOS));
  OPC opc_1 (
    .in_1(C_Bus), .Enable(c_1_out_5), .out_5(B_Bus), .Clock(_2), .B_Enable(n4_16_decoder_1_out_10),
    .Display(OPC));
  Shifter shifter_1 (.C_bus(C_Bus), .Input(n32bit_alu_1_output), .Shifter_Control(alu_under_cs_1_shift));
  _32Bit_ALU u_32bit_alu_1 (
    .B(B_Bus), .A(H), .Output(n32bit_alu_1_output), .Zero(n32bit_alu_1_zero), .Sign(n32bit_alu_1_sign),
    .ALU_Control(alu_under_cs_1_alu));  // open: out_4
  _4_16_Decoder u_4_16_decoder_1 (
    .out_2(n4_16_decoder_1_out_2), .out_3(n4_16_decoder_1_out_3), .out_4(n4_16_decoder_1_out_4),
    .out_5(n4_16_decoder_1_out_5), .out_6(n4_16_decoder_1_out_6), .out_7(n4_16_decoder_1_out_7),
    .out_8(n4_16_decoder_1_out_8), .out_9(n4_16_decoder_1_out_9), .out_10(n4_16_decoder_1_out_10),
    .in_1(b_1_out_3));
  MPC mpc_1 (.out_5({out_1, OP_Code}), .Clock(_4), .Input(junction_box_1_out_5));  // open: Enable, in_1
  Junction_Box junction_box_1 (
    .J(j_1_jmpc), .MBR(MBR), .Addr(addr_1_out_3), .out_5(junction_box_1_out_5), .HB(high_bit_1_out_4));
  High_Bit high_bit_1 (
    .JAMN_JAMZ(j_1_jamn_jamz), .out_4(high_bit_1_out_4), .N(n1_bit_flip_fop_2_out_3),
    .Z(n1_bit_flip_fop_1_out_3));
  _1_bit_flip_fop u_1_bit_flip_fop_1 (.N_Z(n32bit_alu_1_zero), .out_3(n1_bit_flip_fop_1_out_3), .Clock(_3));
  _1_bit_flip_fop u_1_bit_flip_fop_2 (.N_Z(n32bit_alu_1_sign), .out_3(n1_bit_flip_fop_2_out_3), .Clock(_3));
  J j_1 (.Input(J), .JMPC(j_1_jmpc), .JAMN_JAMZ(j_1_jamn_jamz), .Clock(_1));
  Addr addr_1 (.out_3(addr_1_out_3), .in_1(Addr), .Clock(_1));
  Control_Store control_store_1 (.in_1({out_1, OP_Code}), .Addr(Addr), .JAM(J), .ALU(ALU), .C(C), .MEM(M), .B(B));
  ALU_under_CS alu_under_cs_1 (.Input(ALU), .Clock(_1), .ALU(alu_under_cs_1_alu), .Shift(alu_under_cs_1_shift));
  C c_1 (
    .Clock(_1), .in_1(C), .out_11(c_1_out_11), .out_9(c_1_out_9), .out_10(c_1_out_10), .out_8(c_1_out_8),
    .out_7(c_1_out_7), .out_5(c_1_out_5), .out_6(MDR_flag), .out_4(c_1_out_4), .out_3(c_1_out_3));
  M m_1 (.in_1(M), .clock(_1), .out_3(m_1_out_3));
  B b_1 (.in_1(B), .Clock(_1), .out_3(b_1_out_3));
  // Probe on Addr
  // Probe on J
  // Probe on ALU
  // Probe on C
  // Probe on M
  // Probe on B

  // Other names for the same wires on the sheet: OP_Code[8] = out_1

  // Notes on the sheet:
  //   Master Clock
  //   Current OP Code
  //   Registers
  //   1-bit flip flop
  //   MIR
endmodule

module _1_Bit_Adder (
  input  in_1,
  input  in_2,
  input  in_3,
  input  in_4,
  output out_5,
  output out_6
);

  wire and_1_out, and_2_out, xor_1_out, xor_2_out;

  and and_1 (and_1_out, in_3, in_2);
  xor xor_1 (xor_1_out, in_2, in_3);
  or or_1 (out_6, and_1_out, and_2_out);
  and and_2 (and_2_out, xor_1_out, in_1);
  xor xor_2 (xor_2_out, in_1, xor_1_out);
  and and_3 (out_5, xor_2_out, in_4);
endmodule

module _1_Bit_ALU (
  input  in_1,
  input  INVA,
  input  A,
  input  ENA,
  input  B,
  input  ENB,
  input  F0,
  input  F1,
  output Output,
  output out_10
);

  wire and_1_out, and_2_out, and_3_out, and_4_out, and_5_out, and_6_out, and_7_out, and_8_out, and_9_out,
       and_10_out, n1_bit_adder_1_out_5, not_1_out, not_2_out, not_3_out, not_4_out, not_5_out, or_1_out,
       xor_1_out;

  and and_1 (and_1_out, A, ENA);
  and and_2 (and_2_out, B, ENB);
  not not_1 (not_1_out, F0);
  not not_2 (not_2_out, F1);
  not not_3 (not_3_out, F0);
  not not_4 (not_4_out, F1);
  xor xor_1 (xor_1_out, INVA, and_1_out);
  and and_3 (and_3_out, xor_1_out, and_2_out);
  or or_1 (or_1_out, xor_1_out, and_2_out);
  not not_5 (not_5_out, and_2_out);
  and and_4 (and_4_out, not_1_out, not_2_out);
  and and_5 (and_5_out, not_3_out, F1);
  and and_6 (and_6_out, F0, not_4_out);
  and and_7 (and_7_out, F1, F0);
  and and_8 (and_8_out, and_3_out, and_4_out);
  and and_9 (and_9_out, or_1_out, and_5_out);
  and and_10 (and_10_out, not_5_out, and_6_out);
  _1_Bit_Adder u_1_bit_adder_1 (
    .in_2(and_2_out), .in_3(xor_1_out), .in_1(in_1), .out_6(out_10), .out_5(n1_bit_adder_1_out_5),
    .in_4(and_7_out));
  or or_2 (Output, and_8_out, and_9_out, and_10_out, n1_bit_adder_1_out_5);

  // Notes on the sheet:
  //   Ci/INC
endmodule

module _8_Bit_ALU (
  input  [7:0] in_1,
  input  [7:0] in_2,
  input  F1,
  input  F0,
  input  ENB,
  input  ENA,
  input  INVA,
  input  in_8,
  output out_9,
  output [7:0] Output,
  output Zero
);

  wire n1_bit_alu_2_out_10, n1_bit_alu_3_out_10, n1_bit_alu_4_out_10, n1_bit_alu_5_out_10,
       n1_bit_alu_6_out_10, n1_bit_alu_7_out_10, n1_bit_alu_8_out_10;

  _1_Bit_ALU u_1_bit_alu_1 (
    .INVA(INVA), .A(in_2[7]), .ENA(ENA), .B(in_1[7]), .ENB(ENB), .F0(F0), .F1(F1), .Output(Output[7]),
    .in_1(n1_bit_alu_2_out_10), .out_10(out_9));
  _1_Bit_ALU u_1_bit_alu_2 (
    .INVA(INVA), .A(in_2[6]), .ENA(ENA), .B(in_1[6]), .ENB(ENB), .F0(F0), .F1(F1), .Output(Output[6]),
    .in_1(n1_bit_alu_3_out_10), .out_10(n1_bit_alu_2_out_10));
  _1_Bit_ALU u_1_bit_alu_3 (
    .INVA(INVA), .A(in_2[5]), .ENA(ENA), .B(in_1[5]), .ENB(ENB), .F0(F0), .F1(F1), .Output(Output[5]),
    .in_1(n1_bit_alu_4_out_10), .out_10(n1_bit_alu_3_out_10));
  _1_Bit_ALU u_1_bit_alu_4 (
    .INVA(INVA), .A(in_2[4]), .ENA(ENA), .B(in_1[4]), .ENB(ENB), .F0(F0), .F1(F1), .Output(Output[4]),
    .in_1(n1_bit_alu_5_out_10), .out_10(n1_bit_alu_4_out_10));
  _1_Bit_ALU u_1_bit_alu_5 (
    .INVA(INVA), .A(in_2[3]), .ENA(ENA), .B(in_1[3]), .ENB(ENB), .F0(F0), .F1(F1), .Output(Output[3]),
    .in_1(n1_bit_alu_6_out_10), .out_10(n1_bit_alu_5_out_10));
  nor nor_1 (Zero, Output[0], Output[1], Output[2], Output[3], Output[4], Output[5], Output[6], Output[7]);
  _1_Bit_ALU u_1_bit_alu_6 (
    .INVA(INVA), .A(in_2[2]), .ENA(ENA), .B(in_1[2]), .ENB(ENB), .F0(F0), .F1(F1), .Output(Output[2]),
    .in_1(n1_bit_alu_7_out_10), .out_10(n1_bit_alu_6_out_10));
  _1_Bit_ALU u_1_bit_alu_7 (
    .INVA(INVA), .A(in_2[1]), .ENA(ENA), .B(in_1[1]), .ENB(ENB), .F0(F0), .F1(F1), .Output(Output[1]),
    .in_1(n1_bit_alu_8_out_10), .out_10(n1_bit_alu_7_out_10));
  _1_Bit_ALU u_1_bit_alu_8 (
    .INVA(INVA), .A(in_2[0]), .ENA(ENA), .B(in_1[0]), .ENB(ENB), .F0(F0), .F1(F1), .Output(Output[0]),
    .in_1(in_8), .out_10(n1_bit_alu_8_out_10));

  // Notes on the sheet:
  //   A
  //   B
endmodule

module _32Bit_ALU (
  input  [31:0] B,
  input  [31:0] A,
  input  [5:0] ALU_Control,
  output out_4,
  output [31:0] Output,
  output Zero,
  output Sign
);

  wire n8_bit_alu_1_zero, n8_bit_alu_2_out_9, n8_bit_alu_2_zero, n8_bit_alu_3_out_9, n8_bit_alu_3_zero,
       n8_bit_alu_4_out_9, n8_bit_alu_4_zero;
  wire [7:0] and_1_out;

  _8_Bit_ALU u_8_bit_alu_1 (
    .in_2(A[31:24]), .F1(ALU_Control[4]), .ENB(ALU_Control[2]), .ENA(ALU_Control[3]), .INVA(ALU_Control[1]),
    .in_1(B[31:24]), .in_8(n8_bit_alu_2_out_9), .Output(Output[31:24]), .out_9(out_4),
    .Zero(n8_bit_alu_1_zero), .F0(ALU_Control[5]));
  assign and_1_out = 8'h80 & Output[31:24];  // AND_Gate and_1, 8 bits wide
  BitSelector bitselector_1 (.in(and_1_out), .out(Sign), .sel(3'b111));
  and and_2 (Zero, n8_bit_alu_1_zero, n8_bit_alu_2_zero, n8_bit_alu_3_zero, n8_bit_alu_4_zero);
  _8_Bit_ALU u_8_bit_alu_2 (
    .in_2(A[23:16]), .F1(ALU_Control[4]), .ENB(ALU_Control[2]), .ENA(ALU_Control[3]), .INVA(ALU_Control[1]),
    .in_1(B[23:16]), .in_8(n8_bit_alu_3_out_9), .Output(Output[23:16]), .out_9(n8_bit_alu_2_out_9),
    .Zero(n8_bit_alu_2_zero), .F0(ALU_Control[5]));
  _8_Bit_ALU u_8_bit_alu_3 (
    .in_2(A[15:8]), .F1(ALU_Control[4]), .ENB(ALU_Control[2]), .ENA(ALU_Control[3]), .INVA(ALU_Control[1]),
    .in_1(B[15:8]), .in_8(n8_bit_alu_4_out_9), .Output(Output[15:8]), .out_9(n8_bit_alu_3_out_9),
    .Zero(n8_bit_alu_3_zero), .F0(ALU_Control[5]));
  _8_Bit_ALU u_8_bit_alu_4 (
    .in_2(A[7:0]), .F1(ALU_Control[4]), .ENB(ALU_Control[2]), .ENA(ALU_Control[3]), .INVA(ALU_Control[1]),
    .in_1(B[7:0]), .in_8(ALU_Control[0]), .Output(Output[7:0]), .out_9(n8_bit_alu_4_out_9),
    .Zero(n8_bit_alu_4_zero), .F0(ALU_Control[5]));

  // Notes on the sheet:
  //   I
  //   E
  //   E
  //   N
  //   I
  //   N
  //   F
  //   F
  //   N
  //   V
  //   N
  //   1
  //   0
  //   A
  //   B
  //   C
  //   A
endmodule

module Shifter (
  input  [31:0] Input,
  input  [1:0] Shifter_Control,
  output [31:0] C_bus
);

  wire and_1_out, and_2_out, and_3_out, not_1_out, not_2_out, not_3_out, not_4_out;
  wire [31:0] and_5_out, and_6_out, and_7_out, bit_extender_1_out, bit_extender_2_out, bit_extender_3_out,
       shifter_1_out, shifter_2_out;

  not not_1 (not_1_out, Shifter_Control[1]);
  not not_2 (not_2_out, Shifter_Control[0]);
  not not_3 (not_3_out, Shifter_Control[1]);
  not not_4 (not_4_out, Shifter_Control[0]);
  and and_1 (and_1_out, not_1_out, not_2_out);
  and and_2 (and_2_out, not_3_out, Shifter_Control[0]);
  and and_3 (and_3_out, Shifter_Control[1], not_4_out);
  // AND_Gate and_4 has open pins: in0=Shifter_Control[0], in1=Shifter_Control[1], out=open
  assign bit_extender_1_out = {{31{and_1_out}}, and_1_out};  // Bit_Extender bit_extender_1
  assign bit_extender_2_out = {{31{and_2_out}}, and_2_out};  // Bit_Extender bit_extender_2
  assign bit_extender_3_out = {{31{and_3_out}}, and_3_out};  // Bit_Extender bit_extender_3
  Shifter_part #(.width(32), .shift("ar")) shifter_1 (.in(Input), .\dist (5'b00001), .out(shifter_1_out));
  Shifter_part #(.width(32)) shifter_2 (.in(Input), .\dist (5'b01000), .out(shifter_2_out));
  assign and_5_out = bit_extender_1_out & Input;  // AND_Gate and_5, 32 bits wide
  assign and_6_out = bit_extender_2_out & shifter_1_out;  // AND_Gate and_6, 32 bits wide
  assign and_7_out = shifter_2_out & bit_extender_3_out;  // AND_Gate and_7, 32 bits wide
  assign C_bus = and_5_out | and_6_out | and_7_out;  // OR_Gate or_1, 32 bits wide

  // Notes on the sheet:
  //   SRA1
  //   SLL8
endmodule

module RAM (
  input  [31:0] Data,
  input  [23:0] MAR,
  input  [23:0] PC,
  input  Clock,
  input  Read,
  input  Write,
  input  Fetch,
  input  MDR_flag,
  output [31:0] MDR,
  output [7:0] MBR,
  output R_Read
);

  wire and_1_out, and_2_out, and_3_out, not_1_out, or_1_out, or_2_out, or_3_out;
  wire [23:0] controlled_buffer_1_out, controlled_buffer_2_out;
  wire [31:0] controlled_buffer_4_out, controlled_buffer_5_out;

  // Probe on MAR
  // Probe on PC
  and and_1 (and_1_out, Clock, Read);
  and and_2 (and_2_out, Clock, Write);
  and and_3 (and_3_out, Clock, Fetch);
  or or_1 (or_1_out, Write, MDR_flag, Fetch);
  assign controlled_buffer_1_out = or_2_out ? MAR : 24'bz;  // Controlled_Buffer controlled_buffer_1
  or or_2 (or_2_out, and_2_out, and_1_out);
  J_K_Flip_Flop j_k_ff_1 (.J(Read), .clk(and_1_out), .K(Read), .Q(R_Read), .reset(or_1_out));  // open: Qn, preset, en
  assign controlled_buffer_2_out = and_3_out ? PC : 24'bz;  // Controlled_Buffer controlled_buffer_2
  // Probe on Data
  assign controlled_buffer_1_out = Fetch ? {2'b00, controlled_buffer_2_out[23:2]} : 24'bz;  // Controlled_Buffer controlled_buffer_3
  assign controlled_buffer_4_out = Write ? Data : 32'bz;  // Controlled_Buffer controlled_buffer_4
  not not_1 (not_1_out, Write);
  RAM_part #(.addrWidth(24), .dataWidth(32), .bus("asynch")) ram_1 (
    .addr(controlled_buffer_1_out), .data(controlled_buffer_4_out), .ld(or_3_out));  // open: sel, clr
  or or_3 (or_3_out, Read, Fetch);
  assign controlled_buffer_5_out = and_3_out ? controlled_buffer_4_out : 32'bz;  // Controlled_Buffer controlled_buffer_5
  assign MDR = and_1_out ? controlled_buffer_4_out : 32'bz;  // Controlled_Buffer controlled_buffer_6
  // Probe on MDR
  Multiplexer #(.select(2), .width(8)) multiplexer_1 (
    .in0(controlled_buffer_5_out[31:24]), .in1(controlled_buffer_5_out[23:16]),
    .in2(controlled_buffer_5_out[15:8]), .in3(controlled_buffer_5_out[7:0]), .out(MBR),
    .sel(controlled_buffer_2_out[1:0]));  // open: en
  // Probe on MBR
  // Probe on controlled_buffer_5_out[31:24]
  // Probe on controlled_buffer_5_out[23:16]
  // Probe on controlled_buffer_5_out[15:8]
  // Probe on controlled_buffer_5_out[7:0]
endmodule

module MAR (
  input  [31:0] in_1,
  input  in_2,
  input  Clock,
  output [23:0] RamOutput
);

  wire [31:0] register_1_q;

  Register #(.width(32), .trigger("falling")) register_1 (
    .D(in_1), .en(in_2), .Q(register_1_q), .clk(Clock));  // open: clr
  Bit_Extender #(.in_width(32), .out_width(24)) bit_extender_1 (.in(register_1_q), .out(RamOutput));

  // Notes on the sheet:
  //   Input
  //   MAR
endmodule

module MDR (
  input  [31:0] C_Bus,
  input  Enable,
  input  [31:0] R_Output,
  input  B_Enable,
  input  R_Read,
  input  Clock,
  output [31:0] B_Bus,
  output [31:0] R_Input,
  output [31:0] Display
);

  wire [31:0] controlled_buffer_1_out;

  assign controlled_buffer_1_out = R_Read ? R_Output : 32'bz;  // Controlled_Buffer controlled_buffer_1
  assign controlled_buffer_1_out = Enable ? C_Bus : 32'bz;  // Controlled_Buffer controlled_buffer_2
  Register #(.width(32), .trigger("falling")) register_1 (
    .D(controlled_buffer_1_out), .Q(Display), .clk(Clock));  // open: en, clr
  assign B_Bus = B_Enable ? Display : 32'bz;  // Controlled_Buffer controlled_buffer_3

  assign R_Input = Display;

  // Notes on the sheet:
  //   MDR
endmodule

module MBR (
  input  B_Enable,
  input  [7:0] in_2,
  input  Clock,
  input  B_Enable_2,
  output [7:0] Junction_Box,
  output [31:0] out_6,
  output [31:0] out_7
);

  wire [31:0] bit_extender_1_out, bit_extender_2_out;

  Register #(.trigger("falling")) register_1 (.D(in_2), .Q(Junction_Box), .clk(Clock));  // open: en, clr
  assign bit_extender_1_out = {{24{Junction_Box[7]}}, Junction_Box};  // Bit_Extender bit_extender_1
  assign bit_extender_2_out = {{24{1'b0}}, Junction_Box};  // Bit_Extender bit_extender_2
  assign out_6 = B_Enable ? bit_extender_1_out : 32'bz;  // Controlled_Buffer controlled_buffer_1
  assign out_7 = B_Enable_2 ? bit_extender_2_out : 32'bz;  // Controlled_Buffer controlled_buffer_2

  // Notes on the sheet:
  //   8-Bits MBR
  //   Signed
  //   Unsigned
  //   B Bus
  //   B Bus
endmodule

module SP (
  input  [31:0] in_1,
  input  Enable,
  input  Clock,
  input  B_Enable,
  output [31:0] out_5,
  output [31:0] Display
);

  Register #(.width(32), .trigger("falling")) register_1 (
    .D(in_1), .en(Enable), .Q(Display), .clk(Clock));  // open: clr
  assign out_5 = B_Enable ? Display : 32'bz;  // Controlled_Buffer controlled_buffer_1

  // Notes on the sheet:
  //   C Bus
  //   SP
  //   B Bus
endmodule

module LV (
  input  [31:0] in_1,
  input  Enable,
  input  Clock,
  input  B_Enable,
  output [31:0] out_5,
  output [31:0] Display
);

  Register #(.width(32), .trigger("falling")) register_1 (
    .D(in_1), .en(Enable), .Q(Display), .clk(Clock));  // open: clr
  assign out_5 = B_Enable ? Display : 32'bz;  // Controlled_Buffer controlled_buffer_1

  // Notes on the sheet:
  //   C Bus
  //   LV
  //   B Bus
endmodule

module CPP (
  input  [31:0] in_1,
  input  Enable,
  input  Clock,
  input  B_Enable,
  output [31:0] out_5,
  output [31:0] Display
);

  Register #(.width(32), .trigger("falling")) register_1 (
    .D(in_1), .en(Enable), .Q(Display), .clk(Clock));  // open: clr
  assign out_5 = B_Enable ? Display : 32'bz;  // Controlled_Buffer controlled_buffer_1

  // Notes on the sheet:
  //   C Bus
  //   CPP
  //   B Bus
endmodule

module TOS (
  input  [31:0] in_1,
  input  Enable,
  input  Clock,
  input  B_Enable,
  output [31:0] out_5,
  output [31:0] Display
);

  Register #(.width(32), .trigger("falling")) register_1 (
    .D(in_1), .en(Enable), .Q(Display), .clk(Clock));  // open: clr
  assign out_5 = B_Enable ? Display : 32'bz;  // Controlled_Buffer controlled_buffer_1

  // Notes on the sheet:
  //   C Bus
  //   TOS
  //   B Bus
endmodule

module OPC (
  input  [31:0] in_1,
  input  Enable,
  input  Clock,
  input  B_Enable,
  output [31:0] out_5,
  output [31:0] Display
);

  Register #(.width(32), .trigger("falling")) register_1 (
    .D(in_1), .en(Enable), .Q(Display), .clk(Clock));  // open: clr
  assign out_5 = B_Enable ? Display : 32'bz;  // Controlled_Buffer controlled_buffer_1

  // Notes on the sheet:
  //   C Bus
  //   OPC
  //   B Bus
endmodule

module H (
  input  [31:0] in_1,
  input  Enable,
  input  Clock,
  output [31:0] out_4
);

  Register #(.width(32), .trigger("falling")) register_1 (.D(in_1), .en(Enable), .Q(out_4), .clk(Clock));  // open: clr

  // Notes on the sheet:
  //   Input
  //   H
  //   Output
endmodule

module PC (
  input  [31:0] in_1,
  input  Enable,
  input  Clock,
  input  B_Enable,
  output [31:0] Display,
  output [31:0] out_6,
  output [23:0] RamOutput
);

  Register #(.width(32), .trigger("falling")) register_1 (
    .D(in_1), .en(Enable), .Q(Display), .clk(Clock));  // open: clr
  assign out_6 = B_Enable ? Display : 32'bz;  // Controlled_Buffer controlled_buffer_1
  Bit_Extender #(.in_width(32), .out_width(24)) bit_extender_1 (.in(Display), .out(RamOutput));

  // Notes on the sheet:
  //   C Bus
  //   PC
  //   B Bus
endmodule

module _4_16_Decoder (
  input  [3:0] in_1,
  output out_2,
  output out_3,
  output out_4,
  output out_5,
  output out_6,
  output out_7,
  output out_8,
  output out_9,
  output out_10
);

  Decoder #(.select(4)) decoder_1 (
    .out0(out_2), .out1(out_3), .out2(out_4), .out3(out_5), .out4(out_6), .out5(out_7), .out6(out_8),
    .out7(out_9), .out8(out_10), .sel(in_1));  // open: out9, out10, out11, out12, out13, out14, out15, en

  // Notes on the sheet:
  //   4-16 Decoder
endmodule

module High_Bit (
  input  [1:0] JAMN_JAMZ,
  input  N,
  input  Z,
  output out_4
);

  wire and_1_out, and_2_out;

  and and_1 (and_1_out, N, JAMN_JAMZ[1]);
  or or_1 (out_4, and_1_out, and_2_out);
  and and_2 (and_2_out, Z, JAMN_JAMZ[0]);

  // Notes on the sheet:
  //   JAMZ
  //   JAMN
endmodule

module Control_Store (
  input  [8:0] in_1,
  output [8:0] C,
  output [8:0] Addr,
  output [3:0] B,
  output [2:0] MEM,
  output [7:0] ALU,
  output [2:0] JAM
);

  ROM #(.addrWidth(9), .dataWidth(16)) rom_1 (.addr(in_1), .data({C, MEM, B}));  // open: sel
  ROM #(.addrWidth(9), .dataWidth(20)) rom_2 (.addr(in_1), .data({Addr, JAM, ALU}));  // open: sel

  // Notes on the sheet:
  //   contents of rom_1 (hex, n*v repeats v):
  //   0 201 211 8007 2140 8007 2140 8007 2140 8007 2140 147 0 107 84 8000 484 107 c4 211 2000 8005 211
  //   2102 a3 484 211 40 8003 8003 a6 211 8003 8003 218 0 4007 2000 8 211 0 8003 144 480 148 484 145 0 211
  //   2000 40 807 0 0 8005 83 147 4a4 211 2000 27*0 4a4 0 484 5*0 a4 4a4 0 0 0 4a4 8003 211 8003 211 8003
  //   211 403 8003 211 8003 211 8003 211 803 0 0 4*211 5*0 4a4 0 4a4 0 0 0 8005 a3 0 211 8000 211 142 8003
  //   211 8003 211 8003 211 1003 7*0 4a4 0 4a4 4007 2000 8 4a4 484 8020 4007 2000 8 0 0 4001 4*0 4a5 0 8a0
  //   85 210 20 84 800 147 0 211 8003 8003 a6 4001 210 211 8003 8003 211 2004 2087 211 8003 211 5*0 8003
  //   211 8003 211 8003 213 49*0 4011 19*0 211 8003 8003 a5 29*0 211 8003 8003 85
  //   contents of rom_2 (hex, n*v repeats v):
  //   1000 13835 435 2014 103c 3014 103f 4014 100c 5014 101c 1014 6800 1014 7814 8814 b035 9014 a036 e035
  //   1018 c014 b835 19014 c83c d035 d835 18800 e894 f01c c83c 10035 10894 1101c 1183c 1000 12814 13014
  //   914 14035 1000 1501c 1583d 16014 16814 17035 17814 18000 19835 1014 1000 1014 7f000 7f000 1b814
  //   1c03c 1c814 1d036 1d835 1014 27*7f000 6036 7f000 5835 5*7f000 7036 1836 7f000 7f000 7f000 2836 33094
  //   33835 3409c 34835 3509c 35835 101c 36894 37035 3789c 38035 3889c 39035 101c 7f000 7f000 65035 36035
  //   32835 45835 5*7f000 3836 7f000 4836 7f000 7f000 7f000 42814 4383c 7f800 44035 44814 45035 103c 46094
  //   46835 4709c 47835 4809c 48835 101c 7*7f000 12036 7f000 4e036 4e814 4f014 a14 50036 50836 51014 51814
  //   52014 93f 7f000 7f000 f836 4*7f000 56814 57000 57814 58035 58814 59000 59814 5a014 1014 7f000 5b835
  //   5c094 5c81c 5d03c 5d835 5e014 5e835 5f094 5f81c 60035 6083f 61035 61835 14894 80035 5*7f000 65894
  //   66035 6689c 67035 6789c 6801c 1000 47*7f000 1000 f836 19*7f000 8b035 8b894 8c01c c83c 29*7f000 9b835
  //   9c094 9c81c 1c03c 6*7f000
endmodule

module Addr (
  input  [8:0] in_1,
  input  Clock,
  output [8:0] out_3
);

  Register #(.width(9), .trigger("falling")) register_1 (.D(in_1), .Q(out_3), .clk(Clock));  // open: en, clr
endmodule

module J (
  input  [2:0] Input,
  input  Clock,
  output JMPC,
  output [1:0] JAMN_JAMZ
);

  Register #(.width(3), .trigger("falling")) register_1 (
    .D(Input), .Q({JMPC, JAMN_JAMZ}), .clk(Clock));  // open: en, clr
endmodule

module ALU_under_CS (
  input  [7:0] Input,
  input  Clock,
  output [1:0] Shift,
  output [5:0] ALU
);

  Register #(.trigger("falling")) register_1 (.D(Input), .Q({Shift, ALU}), .clk(Clock));  // open: en, clr
endmodule

module C (
  input  [8:0] in_1,
  input  Clock,
  output out_3,
  output out_4,
  output out_5,
  output out_6,
  output out_7,
  output out_8,
  output out_9,
  output out_10,
  output out_11
);

  Register #(.width(9), .trigger("falling")) register_1 (
    .D(in_1), .Q({out_3, out_5, out_7, out_9, out_11, out_10, out_8, out_6, out_4}), .clk(Clock));  // open: en, clr
endmodule

module M (
  input  [2:0] in_1,
  input  clock,
  output [2:0] out_3
);

  Register #(.width(3), .trigger("falling")) register_1 (.D(in_1), .Q(out_3), .clk(clock));  // open: en, clr
endmodule

module B (
  input  [3:0] in_1,
  input  Clock,
  output [3:0] out_3
);

  Register #(.width(4), .trigger("falling")) register_1 (.D(in_1), .Q(out_3), .clk(Clock));  // open: en, clr
  Bit_Extender #(.in_width(9), .out_width(4)) bit_extender_1 ();  // open: in, out
endmodule

module Junction_Box (
  input  [7:0] MBR,
  input  [8:0] Addr,
  input  J,
  input  HB,
  output [8:0] out_5
);

  wire not_1_out;
  wire [7:0] or_1_out;

  assign or_1_out = MBR | Addr[7:0];  // OR_Gate or_1, 8 bits wide
  assign out_5[7:0] = J ? or_1_out : 8'bz;  // Controlled_Buffer controlled_buffer_1
  not not_1 (not_1_out, J);
  assign out_5[7:0] = not_1_out ? Addr[7:0] : 8'bz;  // Controlled_Buffer controlled_buffer_2
  or or_2 (out_5[8], HB, Addr[8]);
endmodule

module MPC (
  input  in_1,
  input  [8:0] Input,
  input  Enable,
  input  Clock,
  output [8:0] out_5
);

  Register #(.width(9), .trigger("falling")) register_1 (.D(Input), .Q(out_5), .clk(Clock));  // open: en, clr

  // Notes on the sheet:
  //   MPC
  //   Output
endmodule

module _1_bit_flip_fop (
  input  Clock,
  input  N_Z,
  output out_3
);

  D_Flip_Flop #(.trigger("falling")) d_ff_1 (.clk(Clock), .D(N_Z), .Q(out_3));  // open: Qn, preset, en, reset
endmodule

module Master_Clock (
  output out_1,
  output out_2,
  output out_3,
  output out_4
);

  wire Clock_out;
  wire [1:0] j_k_ff_2_q;

  Clock Clock (.out(Clock_out));
  Decoder #(.select(2)) decoder_1 (
    .out0(out_1), .out1(out_2), .out2(out_3), .out3(out_4), .sel(j_k_ff_2_q));  // open: en
  J_K_Flip_Flop j_k_ff_1 (
    .J(j_k_ff_2_q[0]), .clk(Clock_out), .K(j_k_ff_2_q[0]), .Q(j_k_ff_2_q[1]));  // open: Qn, preset, en, reset
  J_K_Flip_Flop j_k_ff_2 (.J(1'b1), .clk(Clock_out), .K(1'b1), .Q(j_k_ff_2_q[0]));  // open: Qn, preset, en, reset
  Hex_Digit_Display hex_digit_display_1 (.value({2'b00, j_k_ff_2_q}));  // open: dp
endmodule

module Store (
  input  Clock,
  input  [23:0] I_MAR,
  input  [31:0] I_MDR,
  input  [31:0] I_Data,
  input  [23:0] I_PC,
  input  [7:0] I_MBR,
  output [23:0] O_MAR,
  output [31:0] O_MDR,
  output [31:0] O_Data,
  output [23:0] O_PC,
  output [7:0] O_MBR
);

  Register #(.width(32), .trigger("falling")) register_1 (.D(I_MDR), .Q(O_MDR), .clk(Clock));  // open: en, clr
  Register #(.trigger("falling")) register_2 (.D(I_MBR), .Q(O_MBR), .clk(Clock));  // open: en, clr

  assign O_Data = I_Data;
  assign O_MAR = I_MAR;
  assign O_PC = I_PC;
endmodule
